# Fritzing sketch Circuit diagram (saved by Fritzing 0.9.3b)
circuit board: 8.46667cm x 5.64444cm

parts:
  M1 = fc-51 [package=THT]
  M2 = fc-51 [package=THT]
  U1 = attiny85 [package=dip]
  VCC1 = Battery
  VCC2 = Battery
  J1 = AVR ISP 6 Pin [package=2x3_lock]
  J2 = Basic Servo
  J3 = Basic Servo
  R1 = Resistor [tolerance=±5% resistance=10k package=THT]
  M3 = fc-51 [package=THT]
  C1 = Capacitor Polarized [package=cpol-radial-10uf-25v]
  C2 = Capacitor [package=cap-pth-small-kit]
  D1 = Rectifier Diode [package="Melf DO-213 AA [SMD]"]

nets:
  N1: M1.pin1, U1.Pin_7, J1.3
  GND: M1.pin2, M2.pin2, U1.Pin_4, VCC2.-, J1.6, J2.gnd, J3.gnd, M3.pin2, C1.-, C2.1
  VCC: M1.pin3, M2.pin3, U1.Pin_8, J1.2, J2.vcc, J3.vcc, R1.Pin_0, M3.pin3, C1.+, C2.2, D1.cathode
  N2: M2.pin1, U1.Pin_2
  N3: U1.Pin_1, J1.5, R1.Pin_1
  N4: U1.Pin_3, M3.pin1
  N5: U1.Pin_5, J1.4, J3.pulse
  N6: U1.Pin_6, J1.1, J2.pulse
  N7: VCC1.-, VCC2.+
  N8: VCC1.+, D1.anode
